// Logisim project Assgiment1.circ as structural Verilog: 1 circuit, main circuit main
module main (
  input  in_1
);

  wire and_2_out, and_4_out, and_7_out, and_8_out, and_9_out, and_10_out, and_11_out, and_12_out, and_15_out,
       and_16_out, and_17_out, and_18_out, and_19_out, and_20_out, and_21_out, and_22_out, and_23_out,
       and_24_out, and_25_out, and_26_out, and_27_out, and_28_out, and_29_out, and_30_out, ANDONE_out,
       ANDTWO_out, buffer_1_out, buffer_2_out, buffer_3_out, buffer_4_out, buffer_5_out, buffer_6_out,
       buffer_7_out, buffer_8_out, buffer_9_out, buffer_10_out, buffer_11_out, buffer_12_out, buffer_13_out,
       buffer_14_out, buffer_15_out, buffer_16_out, buffer_17_out, buffer_18_out, buffer_19_out,
       buffer_20_out, buffer_21_out, buffer_22_out, buffer_23_out, buffer_24_out, buffer_25_out,
       buffer_26_out, button_1_out, button_3_out, button_4_out, button_5_out, button_6_out, d_ff_9_q,
       d_ff_10_q, d_ff_11_q, j_k_ff_1_q, j_k_ff_1_qn, nand_1_out, nor_1_out, not_1_out, not_2_out, not_3_out,
       not_4_out, not_5_out, not_6_out, not_7_out, not_8_out, not_9_out, or_1_out, or_5_out, or_6_out,
       or_7_out, or_8_out, or_9_out, or_10_out, or_11_out, or_12_out, or_13_out, or_14_out, xor_1_out,
       xor_2_out, xor_3_out, xor_4_out, xor_5_out;
  wire [2:2] and_1_out;
  wire [3:0] adder_1_out, adder_2_out, and_3_out, and_6_out, and_13_out, and_14_out, d_ff_1_q, d_ff_5_q,
       or_2_out, or_3_out, or_4_out;

  Button button_1 (.out(button_1_out));
  Button button_2 (.out(or_2_out[3]));
  not not_1 (not_1_out, and_10_out);
  and and_1 (and_1_out[2], button_1_out, and_10_out);
  and and_2 (and_2_out, button_1_out, not_1_out);
  or or_1 (or_1_out, and_1_out[2], or_2_out[0]);
  or or_2 (or_2_out[0], and_2_out, or_2_out[3]);
  buf buffer_1 (buffer_1_out, or_1_out);
  buf buffer_2 (buffer_2_out, buffer_1_out);
  buf buffer_3 (buffer_3_out, buffer_2_out);
  buf buffer_4 (buffer_4_out, buffer_3_out);
  buf buffer_5 (buffer_5_out, buffer_4_out);
  buf buffer_6 (buffer_6_out, buffer_5_out);
  buf buffer_7 (buffer_7_out, buffer_6_out);
  buf buffer_8 (buffer_8_out, buffer_7_out);
  assign and_3_out = 4'b1111 & {{3{or_2_out[3]}}, or_2_out[0]};  // AND_Gate and_3, 4 bits wide
  or or_3 (or_3_out[0], and_4_out, or_3_out[3]);
  assign or_4_out = {1'b0, {2{and_1_out[2]}}, 1'b0} | and_3_out;  // OR_Gate or_4, 4 bits wide
  not not_2 (not_2_out, d_ff_1_q[2]);
  buf buffer_9 (buffer_9_out, or_3_out[0]);
  buf buffer_10 (buffer_10_out, buffer_9_out);
  buf buffer_11 (buffer_11_out, buffer_10_out);
  buf buffer_12 (buffer_12_out, buffer_11_out);
  Button button_3 (.out(button_3_out));
  Button button_4 (.out(button_4_out));
  and and_4 (and_4_out, d_ff_1_q[1], not_2_out, d_ff_1_q[3]);
  and and_5 (or_3_out[3], d_ff_1_q[1], d_ff_1_q[2], d_ff_1_q[3]);
  Adder #(.width(4)) adder_1 (.a(d_ff_1_q), .b(or_4_out), .out(adder_1_out));  // open: cin, cout
  buf buffer_13 (buffer_13_out, buffer_12_out);
  buf buffer_14 (buffer_14_out, buffer_13_out);
  buf buffer_15 (buffer_15_out, buffer_14_out);
  buf buffer_16 (buffer_16_out, buffer_15_out);
  not not_3 (not_3_out, d_ff_5_q[2]);
  assign and_6_out = 4'b1111 & {{3{or_3_out[3]}}, or_3_out[0]};  // AND_Gate and_6, 4 bits wide
  and and_7 (and_7_out, d_ff_5_q[1], not_3_out, d_ff_5_q[3]);
  and and_8 (and_8_out, d_ff_5_q[1], d_ff_5_q[2], d_ff_5_q[3]);
  or or_5 (or_5_out, button_3_out, button_4_out);
  D_Flip_Flop d_ff_1 (.D(adder_1_out[0]), .clk(buffer_8_out), .Q(d_ff_1_q[0]), .preset(and_9_out));  // open: Qn, reset
  D_Flip_Flop d_ff_2 (.D(adder_1_out[1]), .clk(buffer_8_out), .Q(d_ff_1_q[1]), .reset(and_4_out));  // open: Qn, preset
  D_Flip_Flop d_ff_3 (
    .D(adder_1_out[2]), .clk(buffer_8_out), .Q(d_ff_1_q[2]), .reset(or_3_out[3]));  // open: Qn, preset
  D_Flip_Flop d_ff_4 (
    .D(adder_1_out[3]), .clk(buffer_8_out), .Q(d_ff_1_q[3]), .preset(or_6_out), .reset(and_4_out));  // open: Qn
  Adder #(.width(4)) adder_2 (.a(d_ff_5_q), .b(and_6_out), .out(adder_2_out));  // open: cin, cout
  and and_9 (and_9_out, or_2_out[3], nor_1_out);
  J_K_Flip_Flop j_k_ff_1 (
    .J(or_5_out), .K(button_4_out), .clk(or_5_out), .Q(j_k_ff_1_q), .Qn(j_k_ff_1_qn), .reset(not_4_out));  // open: preset
  or or_6 (or_6_out, and_9_out, or_3_out[3]);
  D_Flip_Flop d_ff_5 (.D(adder_2_out[0]), .clk(buffer_16_out), .Q(d_ff_5_q[0]), .preset(and_9_out));  // open: Qn, reset
  D_Flip_Flop d_ff_6 (.D(adder_2_out[1]), .clk(buffer_16_out), .Q(d_ff_5_q[1]), .reset(and_7_out));  // open: Qn, preset
  D_Flip_Flop d_ff_7 (.D(adder_2_out[2]), .clk(buffer_16_out), .Q(d_ff_5_q[2]), .reset(and_8_out));  // open: Qn, preset
  D_Flip_Flop d_ff_8 (
    .D(adder_2_out[3]), .clk(buffer_16_out), .Q(d_ff_5_q[3]), .preset(or_7_out), .reset(and_7_out));  // open: Qn
  or or_7 (or_7_out, and_9_out, and_8_out);
  nor nor_1 (nor_1_out, d_ff_5_q[0], d_ff_5_q[1], d_ff_5_q[2], d_ff_5_q[3], d_ff_1_q[0], d_ff_1_q[1], d_ff_1_q[2], d_ff_1_q[3]);
  not not_4 (not_4_out, in_1);
  and and_10 (and_10_out, d_ff_5_q[0], d_ff_5_q[1], d_ff_5_q[2], d_ff_5_q[3], d_ff_1_q[0], d_ff_1_q[1], d_ff_1_q[2], d_ff_1_q[3]);
  and and_11 (and_11_out, in_1, j_k_ff_1_q);
  and and_12 (and_12_out, in_1, j_k_ff_1_qn);
  Hex_Digit_Display hex_digit_display_1 (.value(and_13_out));  // open: dp
  assign and_13_out = d_ff_5_q & {4{in_1}};  // AND_Gate and_13, 4 bits wide
  LED led_1 (.in(and_11_out));
  LED led_2 (.in(and_12_out));
  Hex_Digit_Display hex_digit_display_2 (.value(and_14_out));  // open: dp
  assign and_14_out = d_ff_1_q & {4{in_1}};  // AND_Gate and_14, 4 bits wide
  Button button_5 (.out(button_5_out));
  Button button_6 (.out(button_6_out));
  nand nand_1 (nand_1_out, d_ff_11_q, d_ff_10_q, d_ff_9_q);
  or or_8 (or_8_out, d_ff_10_q, d_ff_11_q, d_ff_9_q);
  and ANDONE (ANDONE_out, nand_1_out, button_5_out);
  and ANDTWO (ANDTWO_out, or_8_out, button_6_out);
  or or_9 (or_9_out, ANDONE_out, ANDTWO_out);
  xor xor_1 (xor_1_out, ANDTWO_out, and_16_out);
  and and_15 (and_15_out, and_16_out, ANDTWO_out);
  xor xor_2 (xor_2_out, ANDTWO_out, or_10_out);
  buf buffer_17 (buffer_17_out, or_9_out);
  buf buffer_18 (buffer_18_out, buffer_17_out);
  buf buffer_19 (buffer_19_out, buffer_18_out);
  buf buffer_20 (buffer_20_out, buffer_19_out);
  buf buffer_21 (buffer_21_out, buffer_20_out);
  buf buffer_22 (buffer_22_out, buffer_21_out);
  buf buffer_23 (buffer_23_out, buffer_22_out);
  xor xor_3 (xor_3_out, d_ff_11_q, xor_2_out);
  buf buffer_24 (buffer_24_out, buffer_23_out);
  buf buffer_25 (buffer_25_out, buffer_24_out);
  buf buffer_26 (buffer_26_out, buffer_25_out);
  and and_16 (and_16_out, or_9_out, d_ff_9_q);
  xor xor_4 (xor_4_out, d_ff_10_q, xor_1_out);
  and and_17 (and_17_out, d_ff_10_q, xor_1_out);
  xor xor_5 (xor_5_out, d_ff_9_q, or_9_out);
  or or_10 (or_10_out, and_17_out, and_15_out);
  D_Flip_Flop d_ff_9 (.D(xor_5_out), .clk(buffer_26_out), .Q(d_ff_9_q));  // open: Qn, preset, reset
  D_Flip_Flop d_ff_10 (.D(xor_4_out), .clk(buffer_26_out), .Q(d_ff_10_q));  // open: Qn, preset, reset
  D_Flip_Flop d_ff_11 (.D(xor_3_out), .clk(buffer_26_out), .Q(d_ff_11_q));  // open: Qn, preset, reset
  not not_5 (not_5_out, d_ff_10_q);
  and and_18 (and_18_out, d_ff_10_q, d_ff_9_q);
  not not_6 (not_6_out, d_ff_11_q);
  not not_7 (not_7_out, d_ff_9_q);
  not not_8 (not_8_out, d_ff_11_q);
  not not_9 (not_9_out, d_ff_9_q);
  and and_19 (and_19_out, d_ff_11_q, d_ff_10_q);
  and and_20 (and_20_out, d_ff_11_q, not_5_out, d_ff_9_q);
  and and_21 (and_21_out, not_6_out, d_ff_10_q, not_7_out);
  and and_22 (and_22_out, not_8_out, d_ff_10_q, not_9_out);
  and and_23 (and_23_out, d_ff_11_q, d_ff_10_q, d_ff_9_q);
  or or_11 (or_11_out, and_19_out, and_20_out);
  or or_12 (or_12_out, d_ff_11_q, and_18_out);
  or or_13 (or_13_out, or_12_out, and_21_out);
  or or_14 (or_14_out, or_13_out, and_22_out);
  and and_24 (and_24_out, and_23_out, in_1);
  LED led_3 (.in(and_24_out));
  and and_25 (and_25_out, and_19_out, in_1);
  LED led_4 (.in(and_25_out));
  and and_26 (and_26_out, or_11_out, in_1);
  LED led_5 (.in(and_26_out));
  and and_27 (and_27_out, d_ff_11_q, in_1);
  LED led_6 (.in(and_27_out));
  and and_28 (and_28_out, or_12_out, in_1);
  LED led_7 (.in(and_28_out));
  and and_29 (and_29_out, or_13_out, in_1);
  and and_30 (and_30_out, or_14_out, in_1);
  LED led_8 (.in(and_29_out));
  LED led_9 (.in(and_30_out));
  LED led_10 (.in(in_1));

  // Notes on the sheet:
  //   >>> Next
  //   <<< Previous 
  //   Play
  //   Pause
  //   Track Number
  //   on/off
  //   PLAY
  //   Pause
  //   Vol+
  //   Vol-
  //   8
  //   7
  //   6
  //   5
  //   4
  //   3
  //   2
  //   1
endmodule
